# Fritzing sketch SparkFun.Bonnet (saved by Fritzing 0.9.3b)
breadboards: 1

parts:
  Raspberry_Pi_Zero1 = Raspberry Pi Zero  # not connected
  IC1 = MCP3008 8-channel 10-bit ADC [part_number=MCP3008]
  Part2 = Soil Moisture Sensor
  KY-1 = Keyes Relay [package=THT]
  Part3 = Lilypad Power Supply
  J2 = Screw terminal - 2 pins [package=THT]
  J3 = Screw terminal - 2 pins [package=THT]
  D1 = Rectifier Diode [package="Melf DO-213 AA [SMD]"]

nets:
  N1: IC1.no_name_yet#1, Part2.SIG
  GND: IC1.no_name_yet#9, IC1.no_name_yet#14, Part2.GND, KY-1.ground, Part3.GND, J2.pin2, J3.pin1
  N2: IC1.no_name_yet#15, IC1.no_name_yet#16, Part2.VCC, KY-1.signal, J3.pin2
  N3: KY-1.C, Part3.+, J2.pin1
  N4: KY-1.NO, D1.anode

notes:
  5v Water pump
  + -
  5v Power Supply
  Raspberry Pi Zero under the Adafruit Bonnet
  Rectifier Diode

custom parts:
  Keyes Relay: The Keyes 5V relay module is suitable for SCM development, home appliance control. It uses a 5V~12V TIL control signal which can control DC / AC signal.
